// Logisim project cpu.circ as structural Verilog: 1 circuit, main circuit main
module main (
  input  [31:0] INSTRUCTION,
  input  CLOCK,
  output [31:0] FETCH_ADDRESS,
  output [31:0] s0_Value,
  output [31:0] s1_Value,
  output [31:0] s2_Value,
  output [31:0] ra_Value,
  output [31:0] sp_Value
);

  wire ALUsrc, and_1_out, equal, MemtoReg, MemWr, nPC_sel, RegDst, RegWr;
  wire [3:0] ALUctr;
  wire [4:0] multiplexer_2_out;
  wire [15:0] IMM16;
  wire [31:0] adder_1_out, adder_2_out, bit_extender_1_out, bit_extender_2_out, main_1_read_data_1,
       main_1_read_data_2, main_2_result, main_3_p5, multiplexer_1_out, multiplexer_3_out, multiplexer_4_out;

  assign bit_extender_1_out = {{16{1'b0}}, IMM16};  // Bit_Extender bit_extender_1
  Adder #(.width(32)) adder_1 (.a(FETCH_ADDRESS), .b(32'h4), .out(adder_1_out));  // open: cin, cout
  Adder #(.width(32)) adder_2 (.a(adder_1_out), .b(bit_extender_1_out), .out(adder_2_out));  // open: cin, cout
  Multiplexer #(.width(32), .enable("false")) multiplexer_1 (
    .in0(adder_1_out), .in1(adder_2_out), .out(multiplexer_1_out), .sel(and_1_out));
  and and_1 (and_1_out, nPC_sel, equal);
  Register #(.width(32)) PC (.D(multiplexer_1_out), .Q(FETCH_ADDRESS), .clk(CLOCK));  // open: en, clr
  Multiplexer #(.width(5)) multiplexer_2 (
    .in0(INSTRUCTION[20:16]), .in1(INSTRUCTION[25:21]), .out(multiplexer_2_out), .sel(RegDst));  // open: en
  regfile_main main_1 (
    .Read_Register_1(INSTRUCTION[15:11]), .Read_Register_2(INSTRUCTION[20:16]),
    .Write_Register(multiplexer_2_out), .Write_Data(multiplexer_4_out), .Write_Enable(RegWr), .Clock(CLOCK),
    .Read_Data_1(main_1_read_data_1), .Read_Data_2(main_1_read_data_2), .s0_Value(s0_Value),
    .s1_Value(s1_Value), .s2_Value(s2_Value), .ra_Value(ra_Value), .sp_Value(sp_Value));
  assign bit_extender_2_out = {{16{1'b0}}, IMM16};  // Bit_Extender bit_extender_2
  Multiplexer #(.width(32), .enable("false")) multiplexer_3 (
    .in0(main_1_read_data_2), .in1(bit_extender_2_out), .out(multiplexer_3_out), .sel(ALUsrc));
  alu_main main_2 (
    .Switch(ALUctr), .X(main_1_read_data_1), .Equal(equal), .Result(main_2_result), .Y(multiplexer_3_out));  // open: Signed_Overflow
  // mem_main main_3: pin names not known; wires that end beside it: main_2_result, main_1_read_data_2, MemWr, CLOCK, main_3_p5
  Multiplexer #(.width(32), .enable("false")) multiplexer_4 (
    .in0(main_2_result), .in1(main_3_p5), .out(multiplexer_4_out), .sel(MemtoReg));

  // Other names for the same wires on the sheet: clk = CLOCK; fetch_addr[31:0] = FETCH_ADDRESS;
  //   RS[4:0] = INSTRUCTION[15:11]; RT[4:0] = INSTRUCTION[20:16]; RD[4:0] = INSTRUCTION[25:21]; ra[31:0] = ra_Value;
  //   s0[31:0] = s0_Value; s1[31:0] = s1_Value; s2[31:0] = s2_Value; sp[31:0] = sp_Value

  // Notes on the sheet:
  //   Output
  //   These are outputs/inputs from run.circ
  //   Inputs
  //   These are DEBUG/TEST outputs from your circuit.
endmodule
